# Fritzing sketch Dispensador (saved by Fritzing 0.9.3b)
breadboards: 2

parts:
  Raspberry_Pi_1 = Raspberry Pi 3 [part_number=RPI-3-V1.2]
  L298N1 = L298N DC motor driver
  M1 = DC Motor  # not connected
  M2 = DC Motor
  Power_plug1 = Power plug  # not connected
  M3 = DC Motor
  U1 = LuaNode32 / ESP32
  Componente1 = RFID-RC522-v2

nets:
  GND: Raspberry_Pi_1.GND, L298N1.GND
  5V: Raspberry_Pi_1.5V, L298N1.5V, L298N1.ENA, L298N1.ENB
  N1: L298N1.OUT1, M3.pin_1
  N2: L298N1.OUT2, M2.pin_1
  GND_2: U1.GND, Componente1.GND
  3V3: U1.3V3, Componente1.3.3V
  N3: U1.D18, Componente1.IRQ
  N4: U1.D19, Componente1.MISO
  N5: U1.D21, Componente1.MOSI
  N6: U1.D22, Componente1.SCK
  N7: U1.D23, Componente1.SDA

custom parts:
  L298N DC motor driver: 2x DC motor driver with 78M05 positive voltage regulator (7..35 V) L298N: max 46 V, 2 A Set 5 V Enable jumper to enable 5 V regultor (needed for the L298N) and +5 V output at screw terminal or supply external +5 V at screw terminal Set ENA and/or ENB to +5 V to enable motor permanently or supply ENA and/or ENB with PWM signal IN1 and IN2 set rotation directory for motor A (OUT1/OUT2) IN2 and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
  LuaNode32 / ESP32: ESP32 based LuaNode32
  RFID-RC522-v2: A simple China made RFID-RC522 Reader; do check the pin labels, as this is a MFRC522 based clone.
